// Logisim project Digital Clock.circ as structural Verilog: 7 circuits, main circuit main
module main (
  input  Off_On
);

  wire button_1_out, button_2_out, button_3_out, button_4_out, button_5_out, button_6_out, clock_1_out,
       motherboard_1_a, motherboard_1_b, motherboard_1_bcd_1_b_1, motherboard_1_bcd_1_b_2,
       motherboard_1_bcd_1_b_3, motherboard_1_bcd_1_t_1, motherboard_1_bcd_1_t_2, motherboard_1_bcd_1_t_3,
       motherboard_1_bcd_1_t_4, motherboard_1_bcd_2_b_1, motherboard_1_bcd_2_b_2, motherboard_1_bcd_2_b_3,
       motherboard_1_bcd_2_t_1, motherboard_1_bcd_2_t_2, motherboard_1_bcd_2_t_3, motherboard_1_bcd_2_t_4,
       motherboard_1_bcd_3_b_1, motherboard_1_bcd_3_b_2, motherboard_1_bcd_3_b_3, motherboard_1_bcd_3_t_1,
       motherboard_1_bcd_3_t_2, motherboard_1_bcd_3_t_3, motherboard_1_bcd_3_t_4, motherboard_1_bcd_4_b_1,
       motherboard_1_bcd_4_b_2, motherboard_1_bcd_4_b_3, motherboard_1_bcd_4_t_1, motherboard_1_bcd_4_t_2,
       motherboard_1_bcd_4_t_3, motherboard_1_bcd_4_t_4, motherboard_1_bcd_5_b_1, motherboard_1_bcd_5_b_2,
       motherboard_1_bcd_5_b_3, motherboard_1_bcd_5_t_1, motherboard_1_bcd_5_t_2, motherboard_1_bcd_5_t_3,
       motherboard_1_bcd_5_t_4, motherboard_1_bcd_6_b_1, motherboard_1_bcd_6_b_2, motherboard_1_bcd_6_b_3,
       motherboard_1_bcd_6_t_1, motherboard_1_bcd_6_t_2, motherboard_1_bcd_6_t_3, motherboard_1_bcd_6_t_4,
       motherboard_1_c, motherboard_1_d, motherboard_1_e, motherboard_1_g;
  wire [1:0] slider_1_out;

  _7_Segment_Display u_7_segment_display_1 (
    .g(motherboard_1_bcd_6_t_1), .f(motherboard_1_bcd_6_t_2), .a(motherboard_1_bcd_6_t_3),
    .b(motherboard_1_bcd_6_t_4), .e(motherboard_1_bcd_6_b_1), .d(motherboard_1_bcd_6_b_2),
    .c(motherboard_1_bcd_6_b_3));  // open: dp
  Button button_1 (.out(button_1_out));
  _7_Segment_Display u_7_segment_display_2 (
    .g(motherboard_1_bcd_5_t_1), .f(motherboard_1_bcd_5_t_2), .a(motherboard_1_bcd_5_t_3),
    .b(motherboard_1_bcd_5_t_4), .e(motherboard_1_bcd_5_b_1), .d(motherboard_1_bcd_5_b_2),
    .c(motherboard_1_bcd_5_b_3));  // open: dp
  _7_Segment_Display u_7_segment_display_3 (
    .g(motherboard_1_bcd_4_t_1), .f(motherboard_1_bcd_4_t_2), .a(motherboard_1_bcd_4_t_3),
    .b(motherboard_1_bcd_4_t_4), .e(motherboard_1_bcd_4_b_1), .d(motherboard_1_bcd_4_b_2),
    .c(motherboard_1_bcd_4_b_3));  // open: dp
  Clock clock_1 (.out(clock_1_out));
  Button button_2 (.out(button_2_out));
  Button button_3 (.out(button_3_out));
  Button button_4 (.out(button_4_out));
  _7_Segment_Display u_7_segment_display_4 (
    .g(motherboard_1_bcd_3_t_1), .f(motherboard_1_bcd_3_t_2), .a(motherboard_1_bcd_3_t_3),
    .b(motherboard_1_bcd_3_t_4), .e(motherboard_1_bcd_3_b_1), .d(motherboard_1_bcd_3_b_2),
    .c(motherboard_1_bcd_3_b_3));  // open: dp
  // Switch switch_1: pin names not known
  Button button_5 (.out(button_5_out));
  _7_Segment_Display u_7_segment_display_5 (
    .g(motherboard_1_bcd_2_t_1), .f(motherboard_1_bcd_2_t_2), .a(motherboard_1_bcd_2_t_3),
    .b(motherboard_1_bcd_2_t_4), .e(motherboard_1_bcd_2_b_1), .d(motherboard_1_bcd_2_b_2),
    .c(motherboard_1_bcd_2_b_3));  // open: dp
  _7_Segment_Display u_7_segment_display_6 (
    .g(motherboard_1_bcd_1_t_1), .f(motherboard_1_bcd_1_t_2), .a(motherboard_1_bcd_1_t_3),
    .b(motherboard_1_bcd_1_t_4), .e(motherboard_1_bcd_1_b_1), .d(motherboard_1_bcd_1_b_2),
    .c(motherboard_1_bcd_1_b_3));  // open: dp
  Button button_6 (.out(button_6_out));
  _7_Segment_Display u_7_segment_display_7 (
    .g(motherboard_1_a), .f(motherboard_1_b), .a(motherboard_1_c), .b(motherboard_1_d), .e(motherboard_1_e),
    .c(motherboard_1_g));  // open: d, dp
  Slider #(.width(2)) slider_1 (.out(slider_1_out));
  // Buzzer buzzer_1: pin names not known
  motherboard motherboard_1 (
    .AL_M10_1(button_6_out), .AL_M6_1(button_5_out), .AL_M10_2(button_4_out), .AL_M6_2(button_3_out),
    .AL_M10_3(button_1_out), .On_Off(Off_On), .Reset_Button(button_2_out), .Clockk(clock_1_out),
    .Mode(slider_1_out), .BCD_2_B_3(motherboard_1_bcd_2_b_3), .BCD_2_B_2(motherboard_1_bcd_2_b_2),
    .BCD_2_B_1(motherboard_1_bcd_2_b_1), .BCD_2_T_2(motherboard_1_bcd_2_t_2),
    .BCD_2_T_3(motherboard_1_bcd_2_t_3), .BCD_2_T_4(motherboard_1_bcd_2_t_4),
    .BCD_3_T_1(motherboard_1_bcd_3_t_1), .BCD_3_B_3(motherboard_1_bcd_3_b_3),
    .BCD_3_B_2(motherboard_1_bcd_3_b_2), .BCD_3_B_1(motherboard_1_bcd_3_b_1),
    .BCD_3_T_2(motherboard_1_bcd_3_t_2), .BCD_3_T_3(motherboard_1_bcd_3_t_3),
    .BCD_3_T_4(motherboard_1_bcd_3_t_4), .BCD_4_T_1(motherboard_1_bcd_4_t_1),
    .BCD_4_B_3(motherboard_1_bcd_4_b_3), .BCD_4_B_2(motherboard_1_bcd_4_b_2),
    .BCD_4_B_1(motherboard_1_bcd_4_b_1), .BCD_4_T_2(motherboard_1_bcd_4_t_2),
    .BCD_4_T_3(motherboard_1_bcd_4_t_3), .BCD_4_T_4(motherboard_1_bcd_4_t_4),
    .BCD_5_T_1(motherboard_1_bcd_5_t_1), .BCD_5_B_3(motherboard_1_bcd_5_b_3),
    .BCD_5_B_2(motherboard_1_bcd_5_b_2), .BCD_5_B_1(motherboard_1_bcd_5_b_1),
    .BCD_5_T_2(motherboard_1_bcd_5_t_2), .BCD_5_T_3(motherboard_1_bcd_5_t_3),
    .BCD_5_T_4(motherboard_1_bcd_5_t_4), .BCD_6_T_1(motherboard_1_bcd_6_t_1),
    .BCD_6_B_3(motherboard_1_bcd_6_b_3), .BCD_6_B_2(motherboard_1_bcd_6_b_2),
    .BCD_6_B_1(motherboard_1_bcd_6_b_1), .BCD_6_T_2(motherboard_1_bcd_6_t_2),
    .BCD_6_T_3(motherboard_1_bcd_6_t_3), .BCD_6_T_4(motherboard_1_bcd_6_t_4), .A(motherboard_1_a),
    .B(motherboard_1_b), .C(motherboard_1_c), .D(motherboard_1_d), .E(motherboard_1_e), .G(motherboard_1_g),
    .BCD_1_T_1(motherboard_1_bcd_1_t_1), .BCD_1_B_3(motherboard_1_bcd_1_b_3),
    .BCD_1_B_2(motherboard_1_bcd_1_b_2), .BCD_1_B_1(motherboard_1_bcd_1_b_1),
    .BCD_1_T_2(motherboard_1_bcd_1_t_2), .BCD_1_T_3(motherboard_1_bcd_1_t_3),
    .BCD_1_T_4(motherboard_1_bcd_1_t_4), .BCD_2_T_1(motherboard_1_bcd_2_t_1));  // open: HR_Format_Switch, AL_Volume, AL_Frequency, One, Buzzer_Toggle

  // Notes on the sheet:
  //   reset
  //   +1
  //   +1
  //   Clock
  //   +1
  //   Stopwatch
  //   24 HR
  //   12 HR
  //   +1
  //   +1
  //   Alarm Set
  //   Timer
endmodule

module motherboard (
  input  Clockk,
  input  HR_Format_Switch,
  input  [1:0] Mode,
  input  On_Off,
  input  Reset_Button,
  input  AL_M10_1,
  input  AL_M6_1,
  input  AL_M10_2,
  input  AL_M6_2,
  input  AL_M10_3,
  output BCD_5_T_2,
  output BCD_5_T_3,
  output BCD_6_T_2,
  output BCD_6_T_3,
  output BCD_2_T_2,
  output BCD_2_T_3,
  output BCD_3_T_2,
  output BCD_3_T_3,
  output BCD_1_T_2,
  output BCD_1_T_3,
  output BCD_4_T_2,
  output BCD_4_T_3,
  output BCD_5_T_1,
  output BCD_5_T_4,
  output BCD_6_T_1,
  output BCD_6_T_4,
  output BCD_2_T_1,
  output BCD_2_T_4,
  output BCD_3_T_1,
  output BCD_3_T_4,
  output BCD_1_T_1,
  output BCD_1_T_4,
  output BCD_4_T_1,
  output BCD_4_T_4,
  output BCD_5_B_3,
  output BCD_6_B_3,
  output BCD_2_B_3,
  output BCD_3_B_3,
  output BCD_1_B_3,
  output BCD_4_B_3,
  output BCD_5_B_2,
  output BCD_6_B_2,
  output BCD_2_B_2,
  output BCD_3_B_2,
  output BCD_1_B_2,
  output BCD_4_B_2,
  output BCD_5_B_1,
  output BCD_6_B_1,
  output BCD_2_B_1,
  output BCD_3_B_1,
  output BCD_1_B_1,
  output BCD_4_B_1,
  output Buzzer_Toggle,
  output One,
  output A,
  output B,
  output C,
  output D,
  output E,
  output G,
  output [6:0] AL_Volume,
  output [13:0] AL_Frequency
);

  wire AL_Time_Reset_12, AL_Time_Reset_24, and_1_out, and_3_out, and_6_out, and_7_out, comparator_1_eq,
       comparator_2_eq, comparator_3_eq, comparator_4_eq, comparator_5_eq, HR_24_out, HR_Constant_out,
       jk_modulo_6_1_o, jk_modulo_6_2_o, jk_modulo_6_4_o, jk_modulo_6_6_o, jk_modulo_6_7_o, jk_modulo_10_1_o,
       jk_modulo_10_2_o, jk_modulo_10_4_o, jk_modulo_10_5_o, jk_modulo_10_7_o, jk_modulo_10_8_o,
       jk_modulo_10_9_o, jk_modulo_10_11_o, multiplexer_2_out, multiplexer_3_out, multiplexer_4_out,
       multiplexer_5_out, multiplexer_6_out, multiplexer_7_out, multiplexer_9_out, multiplexer_10_out,
       multiplexer_11_out, multiplexer_13_out, multiplexer_14_out, multiplexer_15_out, multiplexer_17_out,
       multiplexer_19_out, multiplexer_25_out, multiplexer_26_out, multiplexer_27_out, multiplexer_28_out,
       multiplexer_31_out, multiplexer_36_out, not_1_out, not_2_out, not_3_out, not_4_out, not_5_out,
       not_6_out, not_7_out, not_8_out, not_9_out, not_10_out, not_11_out, not_12_out, not_13_out,
       not_14_out, not_15_out, not_16_out, not_17_out, not_18_out, not_19_out, not_20_out, not_21_out,
       not_22_out, not_23_out, not_24_out, not_25_out, not_26_out, not_27_out, not_28_out, not_29_out,
       not_30_out, not_31_out, not_32_out, not_33_out, not_34_out, not_35_out, not_36_out, not_37_out,
       not_38_out, not_39_out, not_40_out, not_41_out, not_42_out, not_43_out, not_44_out, not_45_out,
       or_1_out, or_2_out, t_ff_1_qn, Time_Reset_12, Time_Reset_24;
  wire [1:0] AL_Modulo_3_24, jk_modulo_2_1_q0;
  wire [2:0] AL_Modulo_6_1, AL_Modulo_6_2, jk_modulo_6_7_q0, SW_Modulo_6_1, SW_Modulo_6_2;
  wire [3:0] AL_Modulo_3_12, AL_Modulo_10_1, AL_Modulo_10_2, AL_Modulo_10_3_12, AL_Modulo_10_3_24,
       bcd_to_7_segment_decoder_1_p5, bcd_to_7_segment_decoder_2_p5, bcd_to_7_segment_decoder_3_p5,
       bcd_to_7_segment_decoder_4_p5, bcd_to_7_segment_decoder_5_p5, bcd_to_7_segment_decoder_6_p5,
       CD_Modulo_6_1, CD_Modulo_10_1, CD_Modulo_10_2, jk_modulo_10_11_q0, Modulo_3_12, Modulo_10_3_12,
       multiplexer_18_out, multiplexer_21_out, multiplexer_22_out, multiplexer_24_out, SW_Modulo_10_1,
       SW_Modulo_10_2, SW_Modulo_10_3, SW_Modulo_10_4;
  wire [19:0] Clock_Time;

  // BCD_to_7_Segment_decoder bcd_to_7_segment_decoder_1: pin names not known; wires that end beside it: BCD_1_T_1, BCD_1_B_1, BCD_1_T_2, BCD_1_B_2, bcd_to_7_segment_decoder_1_p5, BCD_1_T_3, BCD_1_B_3, BCD_1_T_4
  Multiplexer #(.select(2), .width(4)) multiplexer_1 (
    .in0({Clock_Time[0], Clock_Time[3:1]}), .in1(SW_Modulo_10_1), .in2(AL_Modulo_10_1), .in3(CD_Modulo_10_1),
    .out(bcd_to_7_segment_decoder_1_p5), .sel(Mode));
  Multiplexer multiplexer_2 (.in1(Clockk), .out(multiplexer_2_out), .sel(On_Off));  // open: in0
  Multiplexer multiplexer_3 (.in1(Clockk), .out(multiplexer_3_out), .sel(On_Off));  // open: in0
  Multiplexer multiplexer_4 (.in1(AL_M10_1), .out(multiplexer_4_out), .sel(On_Off));  // open: in0
  Multiplexer #(.select(2)) multiplexer_5 (
    .in0(multiplexer_2_out), .out(multiplexer_5_out), .sel(Mode));  // open: in1, in2, in3
  or or_1 (or_1_out, Reset_Button, Time_Reset_24);
  Multiplexer #(.select(2)) multiplexer_6 (
    .in1(multiplexer_3_out), .out(multiplexer_6_out), .sel(Mode));  // open: in0, in2, in3
  Multiplexer #(.select(2)) multiplexer_7 (
    .in2(multiplexer_4_out), .out(multiplexer_7_out), .sel(Mode));  // open: in0, in1, in3
  or or_2 (or_2_out, Reset_Button, AL_Time_Reset_24);
  jk_modulo_10 jk_modulo_10_1 (
    .c(multiplexer_5_out), .r(or_1_out), .q3(Clock_Time[0]), .q2(Clock_Time[3]), .q1(Clock_Time[2]),
    .q0(Clock_Time[1]), .o(jk_modulo_10_1_o));
  jk_modulo_10 jk_modulo_10_2 (
    .c(multiplexer_6_out), .r(Reset_Button), .q3(SW_Modulo_10_1[3]), .q2(SW_Modulo_10_1[2]),
    .q1(SW_Modulo_10_1[1]), .q0(SW_Modulo_10_1[0]), .o(jk_modulo_10_2_o));
  jk_modulo_10 jk_modulo_10_3 (
    .c(multiplexer_7_out), .r(or_2_out), .q3(AL_Modulo_10_1[3]), .q2(AL_Modulo_10_1[2]),
    .q1(AL_Modulo_10_1[1]), .q0(AL_Modulo_10_1[0]));  // open: o
  // BCD_to_7_Segment_decoder bcd_to_7_segment_decoder_2: pin names not known; wires that end beside it: BCD_2_T_1, BCD_2_B_1, BCD_2_T_2, BCD_2_B_2, bcd_to_7_segment_decoder_2_p5, BCD_2_T_3, BCD_2_B_3, BCD_2_T_4
  Multiplexer #(.select(2), .width(4)) multiplexer_8 (
    .in0({1'b0, Clock_Time[6:4]}), .in1({1'b0, SW_Modulo_6_1}), .in2({1'b0, AL_Modulo_6_1}),
    .in3(CD_Modulo_6_1), .out(bcd_to_7_segment_decoder_2_p5), .sel(Mode));
  Multiplexer multiplexer_9 (.in1(AL_M6_1), .out(multiplexer_9_out), .sel(On_Off));  // open: in0
  Multiplexer #(.select(2)) multiplexer_10 (
    .in2(multiplexer_9_out), .out(multiplexer_10_out), .sel(Mode));  // open: in0, in1, in3
  jk_modulo_6 jk_modulo_6_1 (
    .c(jk_modulo_10_1_o), .r(or_1_out), .q2(Clock_Time[6]), .q1(Clock_Time[5]), .q0(Clock_Time[4]),
    .o(jk_modulo_6_1_o));
  jk_modulo_6 jk_modulo_6_2 (
    .c(jk_modulo_10_2_o), .r(Reset_Button), .q2(SW_Modulo_6_1[2]), .q1(SW_Modulo_6_1[1]),
    .q0(SW_Modulo_6_1[0]), .o(jk_modulo_6_2_o));
  Multiplexer multiplexer_11 (.in1(AL_M10_2), .out(multiplexer_11_out), .sel(On_Off));  // open: in0
  jk_modulo_6 jk_modulo_6_3 (
    .c(multiplexer_10_out), .r(or_2_out), .q2(AL_Modulo_6_1[2]), .q1(AL_Modulo_6_1[1]), .q0(AL_Modulo_6_1[0]));  // open: o
  not not_1 (not_1_out, AL_Modulo_10_1[3]);
  not not_2 (not_2_out, AL_Modulo_10_1[0]);
  not not_3 (not_3_out, AL_Modulo_10_1[1]);
  // BCD_to_7_Segment_decoder bcd_to_7_segment_decoder_3: pin names not known; wires that end beside it: BCD_3_T_1, BCD_3_B_1, BCD_3_T_2, BCD_3_B_2, bcd_to_7_segment_decoder_3_p5, BCD_3_T_3, BCD_3_B_3, BCD_3_T_4
  Multiplexer #(.select(2), .width(4)) multiplexer_12 (
    .in0(Clock_Time[10:7]), .in1(SW_Modulo_10_2), .in2(AL_Modulo_10_2), .in3(CD_Modulo_10_2),
    .out(bcd_to_7_segment_decoder_3_p5), .sel(Mode));
  not not_4 (not_4_out, Clock_Time[0]);
  not not_5 (not_5_out, Clock_Time[1]);
  not not_6 (not_6_out, Clock_Time[2]);
  not not_7 (not_7_out, Clock_Time[3]);
  not not_8 (not_8_out, Clock_Time[4]);
  not not_9 (not_9_out, Clock_Time[5]);
  not not_10 (not_10_out, Clock_Time[6]);
  not not_11 (not_11_out, Clock_Time[7]);
  Multiplexer #(.select(2)) multiplexer_13 (
    .in2(multiplexer_11_out), .out(multiplexer_13_out), .sel(Mode));  // open: in0, in1, in3
  not not_12 (not_12_out, AL_Modulo_10_1[2]);
  not not_13 (not_13_out, AL_Modulo_6_1[0]);
  not not_14 (not_14_out, AL_Modulo_6_1[1]);
  not not_15 (not_15_out, AL_Modulo_6_1[2]);
  not not_16 (not_16_out, AL_Modulo_10_2[0]);
  not not_17 (not_17_out, AL_Modulo_10_2[1]);
  not not_18 (not_18_out, AL_Modulo_10_2[2]);
  and and_1 (and_1_out, not_1_out, not_2_out, not_3_out, not_12_out, not_13_out, not_14_out, not_15_out, not_16_out, not_17_out, not_18_out, not_26_out, not_27_out, not_28_out, not_29_out);
  not not_19 (not_19_out, Clock_Time[8]);
  not not_20 (not_20_out, Clock_Time[9]);
  not not_21 (not_21_out, Clock_Time[10]);
  not not_22 (not_22_out, Clock_Time[11]);
  not not_23 (not_23_out, Clock_Time[12]);
  not not_24 (not_24_out, Clock_Time[13]);
  not not_25 (not_25_out, Clock_Time[14]);
  and HR_Constant (HR_Constant_out, not_4_out, not_5_out, not_6_out, not_7_out, not_8_out, not_9_out, not_10_out, not_11_out, not_19_out, not_20_out, not_21_out, not_22_out, not_23_out, not_24_out);
  not not_26 (not_26_out, AL_Modulo_10_2[3]);
  not not_27 (not_27_out, AL_Modulo_6_2[0]);
  not not_28 (not_28_out, AL_Modulo_6_2[1]);
  not not_29 (not_29_out, AL_Modulo_6_2[2]);
  not not_30 (not_30_out, AL_Modulo_10_3_24[3]);
  not not_31 (not_31_out, AL_Modulo_10_3_24[1]);
  not not_32 (not_32_out, AL_Modulo_10_3_24[0]);
  not not_33 (not_33_out, Clock_Time[16]);
  not not_34 (not_34_out, Clock_Time[17]);
  not not_35 (not_35_out, Clock_Time[18]);
  not not_36 (not_36_out, AL_Modulo_3_24[0]);
  jk_modulo_10 jk_modulo_10_4 (
    .c(jk_modulo_6_1_o), .r(or_1_out), .q3(Clock_Time[10]), .q2(Clock_Time[9]), .q1(Clock_Time[8]),
    .q0(Clock_Time[7]), .o(jk_modulo_10_4_o));
  jk_modulo_10 jk_modulo_10_5 (
    .c(jk_modulo_6_2_o), .r(Reset_Button), .q3(SW_Modulo_10_2[3]), .q2(SW_Modulo_10_2[2]),
    .q1(SW_Modulo_10_2[1]), .q0(SW_Modulo_10_2[0]), .o(jk_modulo_10_5_o));
  Multiplexer multiplexer_14 (.in1(AL_M6_2), .out(multiplexer_14_out), .sel(On_Off));  // open: in0
  jk_modulo_10 jk_modulo_10_6 (
    .c(multiplexer_13_out), .r(or_2_out), .q3(AL_Modulo_10_2[3]), .q2(AL_Modulo_10_2[2]),
    .q1(AL_Modulo_10_2[1]), .q0(AL_Modulo_10_2[0]));  // open: o
  and and_2 (Time_Reset_24, HR_Constant_out, HR_24_out);
  and and_3 (and_3_out, not_30_out, AL_Modulo_10_3_24[2], not_31_out, not_32_out, not_36_out, AL_Modulo_3_24[1]);
  and and_4 (AL_Time_Reset_24, and_1_out, and_3_out);
  and HR_24 (HR_24_out, not_25_out, Clock_Time[15], not_33_out, not_34_out, not_35_out, Clock_Time[19]);
  Multiplexer #(.select(2)) multiplexer_15 (
    .in2(multiplexer_14_out), .out(multiplexer_15_out), .sel(Mode));  // open: in0, in1, in3
  // BCD_to_7_Segment_decoder bcd_to_7_segment_decoder_4: pin names not known; wires that end beside it: BCD_4_T_1, BCD_4_B_1, BCD_4_T_2, BCD_4_B_2, bcd_to_7_segment_decoder_4_p5, BCD_4_T_3, BCD_4_B_3, BCD_4_T_4
  Multiplexer #(.select(2), .width(4)) multiplexer_16 (
    .in0({1'b0, Clock_Time[13:11]}), .in1({1'b0, SW_Modulo_6_2}), .in2({1'b0, AL_Modulo_6_2}),
    .out(bcd_to_7_segment_decoder_4_p5), .sel(Mode));  // open: in3
  jk_modulo_6 jk_modulo_6_4 (
    .c(jk_modulo_10_5_o), .r(Reset_Button), .q2(SW_Modulo_6_2[2]), .q1(SW_Modulo_6_2[1]),
    .q0(SW_Modulo_6_2[0]), .o(jk_modulo_6_4_o));
  jk_modulo_6 jk_modulo_6_5 (
    .c(multiplexer_15_out), .r(or_2_out), .q2(AL_Modulo_6_2[2]), .q1(AL_Modulo_6_2[1]), .q0(AL_Modulo_6_2[0]));  // open: o
  jk_modulo_6 jk_modulo_6_6 (
    .c(jk_modulo_10_4_o), .r(or_1_out), .q2(Clock_Time[13]), .q1(Clock_Time[12]), .q0(Clock_Time[11]),
    .o(jk_modulo_6_6_o));
  not not_37 (not_37_out, Modulo_10_3_12[0]);
  not not_38 (not_38_out, Modulo_10_3_12[2]);
  Multiplexer multiplexer_17 (.in1(AL_M10_3), .out(multiplexer_17_out), .sel(On_Off));  // open: in0
  not not_39 (not_39_out, AL_Modulo_10_3_12[0]);
  not not_40 (not_40_out, AL_Modulo_10_3_12[2]);
  not not_41 (not_41_out, AL_Modulo_10_3_12[3]);
  and and_5 (AL_Time_Reset_12, not_39_out, AL_Modulo_10_3_12[1], not_40_out, not_41_out, AL_Modulo_3_12[0], not_44_out);
  not not_42 (not_42_out, Modulo_10_3_12[3]);
  not not_43 (not_43_out, Modulo_3_12[3]);
  and HR_12 (Time_Reset_12, not_37_out, Modulo_10_3_12[1], not_38_out, not_42_out, Modulo_3_12[0], not_43_out);
  not not_44 (not_44_out, AL_Modulo_3_12[3]);
  Multiplexer #(.width(4)) multiplexer_18 (
    .in0({Clock_Time[14], Clock_Time[15], Clock_Time[16], Clock_Time[17]}), .in1(Modulo_10_3_12),
    .out(multiplexer_18_out), .sel(HR_Format_Switch));
  Multiplexer #(.select(2)) multiplexer_19 (
    .in2(multiplexer_17_out), .out(multiplexer_19_out), .sel(Mode));  // open: in0, in1, in3
  jk_modulo_10 jk_modulo_10_7 (
    .c(jk_modulo_6_4_o), .r(Reset_Button), .q3(SW_Modulo_10_3[3]), .q2(SW_Modulo_10_3[2]),
    .q1(SW_Modulo_10_3[1]), .q0(SW_Modulo_10_3[0]), .o(jk_modulo_10_7_o));
  jk_modulo_10 jk_modulo_10_8 (
    .c(multiplexer_19_out), .r(or_2_out), .q3(AL_Modulo_10_3_24[3]), .q2(AL_Modulo_10_3_24[2]),
    .q1(AL_Modulo_10_3_24[1]), .q0(AL_Modulo_10_3_24[0]), .o(jk_modulo_10_8_o));
  jk_modulo_12 jk_modulo_12_1 (
    .c(multiplexer_19_out), .r(AL_Time_Reset_24), .o3_m10(AL_Modulo_10_3_12[3]),
    .o2_m10(AL_Modulo_10_3_12[2]), .o1_m10(AL_Modulo_10_3_12[1]), .o0_m10(AL_Modulo_10_3_12[0]),
    .o1_m3(AL_Modulo_3_12[3]), .o0_m3(AL_Modulo_3_12[0]));
  jk_modulo_10 jk_modulo_10_9 (
    .c(jk_modulo_6_6_o), .r(or_1_out), .q3(Clock_Time[14]), .q2(Clock_Time[15]), .q1(Clock_Time[16]),
    .q0(Clock_Time[17]), .o(jk_modulo_10_9_o));
  jk_modulo_12 jk_modulo_12_2 (
    .c(jk_modulo_6_6_o), .r(Time_Reset_24), .o3_m10(Modulo_10_3_12[3]), .o2_m10(Modulo_10_3_12[2]),
    .o1_m10(Modulo_10_3_12[1]), .o0_m10(Modulo_10_3_12[0]), .o1_m3(Modulo_3_12[3]), .o0_m3(Modulo_3_12[0]));
  // BCD_to_7_Segment_decoder bcd_to_7_segment_decoder_5: pin names not known; wires that end beside it: BCD_5_T_1, BCD_5_B_1, BCD_5_T_2, BCD_5_B_2, bcd_to_7_segment_decoder_5_p5, BCD_5_T_3, BCD_5_B_3, BCD_5_T_4
  Multiplexer #(.select(2), .width(4)) multiplexer_20 (
    .in0(multiplexer_18_out), .in1(SW_Modulo_10_3), .in2(multiplexer_21_out),
    .out(bcd_to_7_segment_decoder_5_p5), .sel(Mode));  // open: in3
  Multiplexer #(.width(4)) multiplexer_21 (
    .in0(AL_Modulo_10_3_24), .in1(AL_Modulo_10_3_12), .out(multiplexer_21_out), .sel(HR_Format_Switch));
  jk_modulo_10 jk_modulo_10_10 (
    .c(jk_modulo_10_7_o), .r(Reset_Button), .q3(SW_Modulo_10_4[3]), .q2(SW_Modulo_10_4[2]),
    .q1(SW_Modulo_10_4[1]), .q0(SW_Modulo_10_4[0]));  // open: o
  jk_modulo_3 jk_modulo_3_1 (
    .c(jk_modulo_10_8_o), .r(or_2_out), .q1(AL_Modulo_3_24[1]), .q0(AL_Modulo_3_24[0]));  // open: o
  Multiplexer #(.width(4)) multiplexer_22 (
    .in0({2'b00, Clock_Time[19:18]}), .in1({{3{Modulo_3_12[3]}}, Modulo_3_12[0]}), .out(multiplexer_22_out),
    .sel(HR_Format_Switch));
  jk_modulo_3 jk_modulo_3_2 (.c(jk_modulo_10_9_o), .r(or_1_out), .q1(Clock_Time[19]), .q0(Clock_Time[18]));  // open: o
  // BCD_to_7_Segment_decoder bcd_to_7_segment_decoder_6: pin names not known; wires that end beside it: BCD_6_T_1, BCD_6_B_1, BCD_6_T_2, BCD_6_B_2, bcd_to_7_segment_decoder_6_p5, BCD_6_T_3, BCD_6_B_3, BCD_6_T_4
  Multiplexer #(.select(2), .width(4)) multiplexer_23 (
    .in0(multiplexer_22_out), .in1(SW_Modulo_10_4), .in2(multiplexer_24_out),
    .out(bcd_to_7_segment_decoder_6_p5), .sel(Mode));  // open: in3
  Multiplexer #(.width(4)) multiplexer_24 (
    .in0({2'b00, AL_Modulo_3_24}), .in1({{3{AL_Modulo_3_12[3]}}, AL_Modulo_3_12[0]}),
    .out(multiplexer_24_out), .sel(HR_Format_Switch));
  Multiplexer multiplexer_25 (.in1(Clockk), .out(multiplexer_25_out), .sel(On_Off));  // open: in0
  Comparator #(.width(20)) comparator_1 (.a({20{1'b0}}), .b(Clock_Time), .eq(comparator_1_eq));  // open: gt, lt
  Comparator #(.width(20)) comparator_2 (
    .a({AL_Modulo_3_24, AL_Modulo_10_3_24[0], AL_Modulo_10_3_24[1], AL_Modulo_10_3_24[2], AL_Modulo_10_3_24[3], AL_Modulo_6_2, AL_Modulo_10_2, AL_Modulo_6_1, AL_Modulo_10_1[2:0], AL_Modulo_10_1[3]}),
    .b(Clock_Time), .eq(comparator_2_eq));  // open: gt, lt
  Multiplexer #(.select(2)) multiplexer_26 (
    .in3(multiplexer_25_out), .out(multiplexer_26_out), .sel(Mode));  // open: in0, in1, in2
  not not_45 (not_45_out, comparator_1_eq);
  Multiplexer #(.select(2)) multiplexer_27 (
    .in0(1'b1), .in2(1'b1), .out(multiplexer_27_out), .sel(Mode));  // open: in1, in3
  and and_6 (and_6_out, not_45_out, comparator_2_eq);
  Multiplexer #(.select(2)) multiplexer_28 (
    .in0(and_6_out), .in3(and_7_out), .out(multiplexer_28_out), .sel(Mode));  // open: in1, in2
  Multiplexer multiplexer_29 (.in1(multiplexer_27_out), .out(A), .sel(HR_Format_Switch));  // open: in0
  jk_modulo_10 jk_modulo_10_11 (
    .c(multiplexer_26_out), .r(Reset_Button), .q3(jk_modulo_10_11_q0[3]), .q2(jk_modulo_10_11_q0[2]),
    .q1(jk_modulo_10_11_q0[1]), .q0(jk_modulo_10_11_q0[0]), .o(jk_modulo_10_11_o));
  jk_modulo_6 jk_modulo_6_7 (
    .c(jk_modulo_10_11_o), .r(Reset_Button), .q2(jk_modulo_6_7_q0[2]), .q1(jk_modulo_6_7_q0[1]),
    .q0(jk_modulo_6_7_q0[0]), .o(jk_modulo_6_7_o));
  jk_modulo_2 jk_modulo_2_1 (.c(jk_modulo_6_7_o), .r(Reset_Button), .q1(jk_modulo_2_1_q0[1]), .q0(jk_modulo_2_1_q0[0]));
  Multiplexer multiplexer_30 (.in1(multiplexer_28_out), .out(Buzzer_Toggle), .sel(On_Off));  // open: in0
  Multiplexer #(.select(2)) multiplexer_31 (
    .in0(Time_Reset_12), .in2(AL_Time_Reset_12), .out(multiplexer_31_out), .sel(Mode));  // open: in1, in3
  Multiplexer multiplexer_32 (.in1(multiplexer_27_out), .out(B), .sel(HR_Format_Switch));  // open: in0
  Multiplexer multiplexer_33 (.in1(multiplexer_27_out), .out(C), .sel(HR_Format_Switch));  // open: in0
  T_Flip_Flop t_ff_1 (.T(multiplexer_27_out), .clk(multiplexer_31_out), .Qn(t_ff_1_qn));  // open: Q, reset, preset
  Subtractor #(.width(4)) subtractor_1 (.a(4'b1001), .b(jk_modulo_10_11_q0), .out(CD_Modulo_10_1));  // open: bin, bout
  Subtractor #(.width(4)) subtractor_2 (
    .a(4'b0101), .b({1'b0, jk_modulo_6_7_q0}), .out(CD_Modulo_6_1));  // open: bin, bout
  Subtractor #(.width(4)) subtractor_3 (
    .a(4'b0001), .b({2'b00, jk_modulo_2_1_q0}), .out(CD_Modulo_10_2));  // open: bin, bout
  Multiplexer multiplexer_34 (.in1(multiplexer_27_out), .out(D), .sel(HR_Format_Switch));  // open: in0
  Multiplexer multiplexer_35 (.in1(multiplexer_27_out), .out(E), .sel(HR_Format_Switch));  // open: in0
  Comparator #(.width(4)) comparator_3 (.a(4'b0000), .b(CD_Modulo_10_1), .eq(comparator_3_eq));  // open: gt, lt
  Comparator #(.width(4)) comparator_4 (.a(4'b0000), .b(CD_Modulo_6_1), .eq(comparator_4_eq));  // open: gt, lt
  Comparator #(.width(4)) comparator_5 (.a(4'b0000), .b(CD_Modulo_10_2), .eq(comparator_5_eq));  // open: gt, lt
  Multiplexer #(.select(2)) multiplexer_36 (
    .in0(t_ff_1_qn), .in2(t_ff_1_qn), .out(multiplexer_36_out), .sel(Mode));  // open: in1, in3
  Multiplexer multiplexer_37 (.in1(multiplexer_36_out), .out(G), .sel(HR_Format_Switch));  // open: in0
  and and_7 (and_7_out, comparator_3_eq, comparator_4_eq, comparator_5_eq);

  assign AL_Frequency = 14'h600;
  assign AL_Volume = {7{1'b1}};
  assign One = 1'b1;
  // also tied to GND on the sheet: {AL_Modulo_3_12[3], Modulo_3_12[3]}

  // Other names for the same wires on the sheet: AL_Modulo_3_12[2:1] = {2{AL_Modulo_3_12[3]}};
  //   Alarm_Time[19:0] = {AL_Modulo_3_24, AL_Modulo_10_3_24[0], AL_Modulo_10_3_24[1], AL_Modulo_10_3_24[2], AL_Modulo_10_3_24[3], AL_Modulo_6_2, AL_Modulo_10_2, AL_Modulo_6_1, AL_Modulo_10_1[2:0], AL_Modulo_10_1[3]};
  //   Clock = Clockk; Modulo_10_1[3:0] = {Clock_Time[0], Clock_Time[3:1]}; HR_Format = HR_Format_Switch;
  //   Modulo_3_12[2:1] = {2{Modulo_3_12[3]}}; Modulo_3_24[1:0] = Clock_Time[19:18]; Modulo_6_1[2:0] = Clock_Time[6:4];
  //   Modulo_6_2[2:0] = Clock_Time[13:11]; Modulo_10_2[3:0] = Clock_Time[10:7];
  //   Modulo_10_3_24[3:0] = {Clock_Time[14], Clock_Time[15], Clock_Time[16], Clock_Time[17]}
endmodule

module jk_modulo_12 (
  input  c,
  input  r,
  output o3_m10,
  output o2_m10,
  output o1_m10,
  output o0_m10,
  output o1_m3,
  output o0_m3
);

  wire and_1_out, and_2_out, and_3_out, and_4_out, and_5_out, and_6_out, and_7_out, and_8_out, not_1_out,
       not_2_out, not_3_out, not_4_out, not_5_out, not_6_out, not_7_out, not_8_out, not_9_out, not_10_out,
       q1, q3;

  and and_1 (and_1_out, q1, o0_m10);
  and and_2 (and_2_out, o2_m10, q1, o0_m10);
  J_K_Flip_Flop j_k_ff_1 (.J(and_2_out), .K(and_1_out), .clk(c), .Q(q3), .reset(r));  // open: Qn, preset
  not not_1 (not_1_out, q3);
  and and_3 (and_3_out, not_1_out, q1, o0_m10);
  and and_4 (and_4_out, q1, o0_m10);
  J_K_Flip_Flop j_k_ff_2 (.J(and_3_out), .K(and_4_out), .clk(c), .Q(o2_m10), .reset(r));  // open: Qn, preset
  J_K_Flip_Flop j_k_ff_3 (.J(o0_m10), .K(o0_m10), .clk(c), .Q(q1), .reset(r));  // open: Qn, preset
  J_K_Flip_Flop j_k_ff_4 (.J(1'b1), .K(1'b1), .clk(c), .Q(o0_m10), .reset(r));  // open: Qn, preset
  not not_2 (not_2_out, q3);
  not not_3 (not_3_out, o2_m10);
  not not_4 (not_4_out, o0_m10);
  not not_5 (not_5_out, q3);
  not not_6 (not_6_out, o0_m10);
  not not_7 (not_7_out, q1);
  not not_8 (not_8_out, o2_m10);
  not not_9 (not_9_out, q3);
  _7_Segment_Display u_7_segment_display_1 ();  // open: g, f, a, b, e, d, c, dp
  // BCD_to_7_Segment_decoder bcd_to_7_segment_decoder_1: pin names not known; wires that end beside it: {q3, o2_m10, q1, o0_m10}
  not not_10 (not_10_out, q1);
  and and_5 (and_5_out, not_2_out, not_3_out, not_4_out);
  and and_6 (and_6_out, not_5_out, q1);
  and and_7 (and_7_out, not_6_out, not_7_out, not_8_out, not_9_out);
  and and_8 (and_8_out, q3, q1);
  and and_9 (o3_m10, q3, not_10_out);
  or or_1 (o1_m10, and_5_out, and_6_out);
  or or_2 (o0_m3, and_7_out, and_8_out);
  _7_Segment_Display u_7_segment_display_2 ();  // open: g, f, a, b, e, d, c, dp
  // BCD_to_7_Segment_decoder bcd_to_7_segment_decoder_2: pin names not known; wires that end beside it: {3'b000, o0_m3}
  _7_Segment_Display u_7_segment_display_3 ();  // open: g, f, a, b, e, d, c, dp
  // BCD_to_7_Segment_decoder bcd_to_7_segment_decoder_3: pin names not known; wires that end beside it: {o3_m10, o2_m10, o1_m10, o0_m10}

  assign o1_m3 = 1'b0;

  // Other names for the same wires on the sheet: q0 = o0_m10; q2 = o2_m10
endmodule

module jk_modulo_10 (
  input  c,
  input  r,
  output q3,
  output q2,
  output q1,
  output q0,
  output o
);

  wire and_1_out, and_2_out, and_3_out, and_4_out, not_1_out, not_2_out, not_3_out;

  J_K_Flip_Flop j_k_ff_1 (.J(and_1_out), .K(q0), .clk(c), .Q(q3), .reset(r));  // open: Qn, preset
  and and_1 (and_1_out, q2, and_2_out);
  J_K_Flip_Flop j_k_ff_2 (.J(and_2_out), .K(and_2_out), .clk(c), .Q(q2), .reset(r));  // open: Qn, preset
  and and_2 (and_2_out, q1, q0);
  not not_1 (not_1_out, q2);
  J_K_Flip_Flop j_k_ff_3 (.J(and_3_out), .K(q0), .clk(c), .Q(q1), .reset(r));  // open: Qn, preset
  not not_2 (not_2_out, q1);
  J_K_Flip_Flop j_k_ff_4 (.J(1'b1), .K(1'b1), .clk(c), .Q(q0), .reset(r));  // open: Qn, preset
  and and_3 (and_3_out, q0, not_3_out);
  not not_3 (not_3_out, q3);
  and and_4 (and_4_out, q0, not_2_out, not_1_out, q3);
  D_Flip_Flop d_ff_1 (.D(and_4_out), .clk(c), .Q(o));  // open: Qn, preset, reset
endmodule

module jk_modulo_6 (
  input  c,
  input  r,
  output q2,
  output q1,
  output q0,
  output o
);

  wire and_1_out, and_2_out, and_3_out, j_k_ff_2_qn, not_1_out;

  J_K_Flip_Flop j_k_ff_1 (.J(and_1_out), .K(q0), .clk(c), .Q(q2), .reset(r));  // open: Qn, preset
  J_K_Flip_Flop j_k_ff_2 (.J(and_3_out), .K(q0), .clk(c), .Q(q1), .Qn(j_k_ff_2_qn), .reset(r));  // open: preset
  J_K_Flip_Flop j_k_ff_3 (.J(1'b1), .K(1'b1), .clk(c), .Q(q0), .reset(r));  // open: Qn, preset
  and and_1 (and_1_out, q1, q0);
  and and_2 (and_2_out, q2, j_k_ff_2_qn, q0);
  and and_3 (and_3_out, q0, not_1_out);
  not not_1 (not_1_out, q2);
  D_Flip_Flop d_ff_1 (.D(and_2_out), .clk(c), .Q(o));  // open: Qn, preset, reset
endmodule

module jk_modulo_3 (
  input  c,
  input  r,
  output q1,
  output q0,
  output o
);

  wire j_k_ff_1_qn, j_k_ff_2_qn;

  J_K_Flip_Flop j_k_ff_1 (.J(q0), .K(q0), .clk(c), .Q(q1), .Qn(j_k_ff_1_qn), .reset(r));  // open: preset
  J_K_Flip_Flop j_k_ff_2 (.J(1'b1), .K(1'b1), .clk(c), .Q(q0), .Qn(j_k_ff_2_qn), .reset(r));  // open: preset
  and and_1 (o, j_k_ff_2_qn, j_k_ff_1_qn);
endmodule

module jk_modulo_2 (
  input  c,
  input  r,
  output q1,
  output q0
);

  wire not_1_out;

  J_K_Flip_Flop j_k_ff_1 (.J(q0), .K(1'b1), .clk(c), .Q(q1), .reset(r));  // open: Qn, preset
  J_K_Flip_Flop j_k_ff_2 (.J(not_1_out), .K(1'b1), .clk(c), .Q(q0), .reset(r));  // open: Qn, preset
  not not_1 (not_1_out, q1);
endmodule
